# Fritzing sketch motor (saved by Fritzing 0.9.2b)
breadboards: 1

parts:
  Part1 = Arduino Nano (Rev3.0)
  Motor = DC Motor
  Battery = LIPO-110mAh [package=lipo-110]
  Screw_Terminal_(B) = Screw terminal - 2 pins [package=THT]

nets:
  B-1A: Part1.D6
  B-1B: Part1.D7
  N1: Motor.pin_1, Screw_Terminal_(B).pin1
  N2: Motor.pin_2, Screw_Terminal_(B).pin2
  VCC: Battery.+
  GND: Battery.-
